// Logisim project simple_prescaler.circ as structural Verilog: 1 circuit, main circuit main
module main (
  input  WDE,
  input  [1:0] WDP0_1,
  input  WDIE
);

  wire and_1_out, and_2_out, button_1_out, clock_1_out, comparator_1_eq, comparator_1_gt, counter_2_carry,
       d_ff_1_q, nand_1_out, not_1_out, or_1_out;
  wire [8:0] counter_1_q, multiplexer_1_out;

  Clock clock_1 (.out(clock_1_out));
  Counter #(.width(9), .max('h1ff)) counter_1 (
    .Q(counter_1_q), .clk(clock_1_out), .clr(or_1_out));  // open: load, D, count, carry
  Multiplexer #(.select(2), .width(9)) multiplexer_1 (
    .in1(9'ha), .in3(9'h32), .out(multiplexer_1_out), .sel(WDP0_1));  // open: in0, in2, en
  Comparator #(.width(9)) comparator_1 (
    .a(counter_1_q), .b(multiplexer_1_out), .gt(comparator_1_gt), .eq(comparator_1_eq));  // open: lt
  or or_1 (or_1_out, comparator_1_gt, comparator_1_eq);
  Counter #(.width(9), .max('h8)) counter_2 (.carry(counter_2_carry), .clk(or_1_out));  // open: load, D, count, Q, clr
  nand nand_1 (nand_1_out, WDE, d_ff_1_q);
  Button button_1 (.out(button_1_out));
  and and_1 (and_1_out, WDE, counter_2_carry, not_1_out);
  not not_1 (not_1_out, and_2_out);
  and and_2 (and_2_out, nand_1_out, WDIE);
  D_Flip_Flop d_ff_1 (.clk(counter_2_carry), .D(1'b1), .Q(d_ff_1_q), .reset(button_1_out));  // open: Qn, preset, en
  LED led_1 (.in(and_1_out));
  LED led_2 (.in(and_2_out));

  // Notes on the sheet:
  //   тактовий генератор
  //   1/10
  //   1/50
  //   WDIF
  //   reset MCU
  //   interrupt
  //   стався тайм-аут
endmodule
